# Fritzing sketch proyecto-fritzing (saved by Fritzing 0.9.3b)
breadboards: 1

parts:
  Componente1 = Arduino Uno (Rev3)
  S1 = Pushbutton [package="[THT]"]
  S2 = Pushbutton [package="[THT]"]
  S3 = Pushbutton [package="[THT]"]
  S4 = Pushbutton [package="[THT]"]
  Componente2 = Thumb Joystick

nets:
  N1: Componente1.A2, Componente2.HORZ
  N2: Componente1.A3, Componente2.VERT
  N3: Componente1.D3_PWM, S1.Pin_3, S1.Pin_4
  N4: Componente1.D4, S3.Pin_3, S3.Pin_4
  N5: Componente1.D5_PWM, S2.Pin_3, S2.Pin_4
  N6: Componente1.D6_PWM, S4.Pin_3, S4.Pin_4
  5V: Componente1.5V, Componente2.VCC
  GND: Componente1.GND, Componente2.GND
  N7: S1.Pin_1, S1.Pin_2, S2.Pin_1, S2.Pin_2, S3.Pin_1, S3.Pin_2
  N8: S4.Pin_1, S4.Pin_2

notes:
  Conexion de componentes en Arduino UNO
